# Fritzing sketch OBR2026back (saved by Fritzing 1.0.5)
circuit board: 12cm x 15cm
breadboards: 1

parts:
  Cores = female pin header, 7 pins [form="♀ (female)"]
  Cores_2 = female pin header, 7 pins [form="♀ (female)"]
  Distancia = female pin header, 6 pins [form="♀ (female)"]
  Distancia_G = female pin header, 6 pins [form="♀ (female)"]
  Distancia_2 = female pin header, 6 pins [form="♀ (female)"]
  M1 = female pin header, 6 pins [form="♀ (female)"]
  M2 = female pin header, 6 pins [form="♀ (female)"]
  M3 = female pin header, 6 pins [form="♀ (female)"]
  M4 = female pin header, 6 pins [form="♀ (female)"]
  Bateria = Battery [internal_resistance=0.1Ω]
  Garra_C = female pin header, 7 pins [form="♀ (female)"]
  Nano = Arduino Nano (Rev3.0)
  Giroscopico = MPU-6050 Board GY-521 [form="♀ (female)" package=THT]
  S1 = Basic Servo
  S2 = Basic Servo
  Linhas = female pin header, 3 pins [form="♀ (female)"]
  Linhas_2 = female pin header, 3 pins [form="♀ (female)"]
  Linhas_3 = female pin header, 3 pins [form="♀ (female)"]
  Linhas_4 = female pin header, 3 pins [form="♀ (female)"]
  Multi_I2c = Adafruit TCA9548A
  Mod1 = infrared 4 channels
  PonteH = Ponte H Mini
  +-_Ponte_H = Battery [internal_resistance=0.1Ω]

nets:
  GND: Cores.pin2, Cores_2.pin2, Distancia.pin5, Distancia_G.pin5, Distancia_2.pin5, M1.pin2, M2.pin2, M3.pin5, M4.pin5, Bateria.-, Garra_C.pin2, Nano.GND, Giroscopico.pin2, S1.gnd, S2.gnd, Multi_I2c.GND, Mod1.GND#13
  3.3V: Cores.pin3, Cores_2.pin3, Distancia.pin6, Distancia_G.pin6, Distancia_2.pin6, M1.pin5, M2.pin5, M3.pin2, M4.pin2, Bateria.+, Garra_C.pin3, Nano.3V3, Giroscopico.pin1, S1.vcc, S2.vcc, Multi_I2c.VCC, Mod1.VCC#14
  SCL6: Cores.pin4, Multi_I2c.6SCL
  SDA6: Cores.pin5, Multi_I2c.6SDA
  SCL7: Cores_2.pin4, Multi_I2c.7SCL
  SDA7: Cores_2.pin5, Multi_I2c.7SDA
  SDA5: Distancia.pin3, Multi_I2c.5SDA
  SCL5: Distancia.pin4, Multi_I2c.5SCL
  SDA4: Distancia_G.pin3, Multi_I2c.4SDA
  SCL4: Distancia_G.pin4, Multi_I2c.4SCL
  SDA0: Distancia_2.pin3, Multi_I2c.0SDA
  SCL0: Distancia_2.pin4, Multi_I2c.0SCL
  MOTOR-A1: M1.pin1, M2.pin1, PonteH.MotorA1
  D2: M1.pin3, Nano.D2
  MOTOR-A2: M1.pin6, M2.pin6, PonteH.MotorA2
  MOTOR-B1: M3.pin1, M4.pin1, PonteH.MotorB1
  D3: M3.pin4, Nano.D3
  MOTOR-B2: M3.pin6, M4.pin6, PonteH.MotorB2
  SCL3: Garra_C.pin4, Multi_I2c.3SCL
  SDA3: Garra_C.pin5, Multi_I2c.3SDA
  D1/TX: Nano.D1/TX, S1.pulse
  D0/RX: Nano.D0/RX, S2.pulse
  D6: Nano.D6, PonteH.in1
  D8: Nano.D8
  D9: Nano.D9, PonteH.in2
  D10: Nano.D10, PonteH.in3
  D11: Nano.D11/MOSI, PonteH.in4
  OUT4: Nano.A7, Mod1.OUT4
  OUT3: Nano.A6, Mod1.OUT3
  A5: Nano.A5, Multi_I2c.INPUTSCL
  A4: Nano.A4, Multi_I2c.INPUTSDA
  OUT2: Nano.A3, Mod1.OUT2
  OUT1: Nano.A2, Mod1.OUT1
  SCL1: Giroscopico.pin3, Multi_I2c.1SCL
  SDA1: Giroscopico.pin4, Multi_I2c.1SDA
  IN1: Linhas.pin1, Mod1.IN1
  GND1: Linhas.pin2, Mod1.GND#9
  VIN1: Linhas.pin3, Mod1.VCC#15
  IN2: Linhas_2.pin1, Mod1.IN2
  GND2: Linhas_2.pin2, Mod1.GND#10
  VIN2: Linhas_2.pin3, Mod1.VCC#16
  VIN3: Linhas_3.pin1, Mod1.VCC#18
  GND3: Linhas_3.pin2, Mod1.GND#12
  IN3: Linhas_3.pin3, Mod1.IN3
  VIN4: Linhas_4.pin1, Mod1.VCC#17
  GND4: Linhas_4.pin2, Mod1.GND#11
  IN4: Linhas_4.pin3, Mod1.IN4
  SDA2: Multi_I2c.2SDA
  SCL2: Multi_I2c.2SCL
  GND PONTE H: PonteH.GND, +-_Ponte_H.-
  VTD PONTE H: PonteH.VTD, +-_Ponte_H.+

custom parts:
  MPU-6050 Board GY-521: Acelerometro y Giroscopio MPU-6050 Board GY-521
  Adafruit TCA9548A: You just found the perfect I2C sensor, and you want to wire up two or three or more of them to your Arduino when you realize "Uh oh, this chip has a fixed I2C address, and from what I know about I2C, you cannot have two devices with the same address on the same SDA/SCL pins!" Are you out of luck? You would be, if you didn't have this ultra-cool TCA9548A 1-to-8 I2C multiplexer! Finally, a way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
